// Logisim project circuit.circ as structural Verilog: 12 circuits, main circuit decoder
module main (
  input  CLR,
  output [3:0] High,
  output [3:0] LOW
);

  wire Clk_out, controlled_buffer_4_out, controller_1_cp, controller_1_ea, controller_1_ep, controller_1_eu,
       controller_1_hlt, controller_1_nce, controller_1_ne1, controller_1_nl1, controller_1_nla,
       controller_1_nlb, controller_1_nlm, controller_1_nlo, controller_1_su, not_1_out, not_2_out,
       not_3_out, not_4_out, not_5_out, not_6_out, not_7_out, not_8_out;
  wire [3:0] IR_output, IR_output_2, mar_final_1_out;
  wire [7:0] adder_1_output, bit_extender_1_out, reg_final_1_output, reg_final_2_output, reg_final_3_output,
       xor_1_out;

  not not_1 (not_1_out, controller_1_nlm);
  not not_2 (not_2_out, controller_1_nl1);
  pc pc_1 (.CP(controller_1_cp), .EP(controller_1_ep), .CLR(CLR), .CLK(controlled_buffer_4_out), .\output (LOW));
  MAR_FINAL mar_final_1 (.IN(LOW), .ENABLE(not_1_out), .CLK(controlled_buffer_4_out), .CLR(CLR), .OUT(mar_final_1_out));
  not not_3 (not_3_out, controller_1_nce);
  REG_FINAL IR (
    .INPUT({High, LOW}), .ENABLE(not_2_out), .CLK(controlled_buffer_4_out), .CLR(CLR),
    .OUTPUT({IR_output_2, IR_output}));
  CONTROLLER controller_1 (
    .CLK(controlled_buffer_4_out), .I7(IR_output_2[3]), .I6(IR_output_2[2]), .I5(IR_output_2[1]),
    .I4(IR_output_2[0]), .HLT(controller_1_hlt), .CP(controller_1_cp), .EP(controller_1_ep),
    .nLM(controller_1_nlm), .nCE(controller_1_nce), .nL1(controller_1_nl1), .nE1(controller_1_ne1),
    .nLA(controller_1_nla), .EA(controller_1_ea), .SU(controller_1_su), .EU(controller_1_eu),
    .nLB(controller_1_nlb), .nLO(controller_1_nlo), .CLR(CLR));
  RAM #(.addrWidth(4)) ram_1 (.addr(mar_final_1_out), .data({High, LOW}), .ld(not_3_out));  // open: sel, clk, clr
  not not_4 (not_4_out, controller_1_ne1);
  assign LOW = not_4_out ? IR_output : 4'bz;  // Controlled_Buffer controlled_buffer_1
  not not_5 (not_5_out, controller_1_nla);
  assign {High, LOW} = controller_1_ea ? reg_final_1_output : 8'bz;  // Controlled_Buffer controlled_buffer_2
  assign {High, LOW} = controller_1_eu ? adder_1_output : 8'bz;  // Controlled_Buffer controlled_buffer_3
  not not_6 (not_6_out, controller_1_nlb);
  not not_7 (not_7_out, controller_1_nlo);
  REG_FINAL reg_final_1 (
    .INPUT({High, LOW}), .ENABLE(not_5_out), .CLK(controlled_buffer_4_out), .CLR(CLR),
    .OUTPUT(reg_final_1_output));
  adder adder_1 (.cin(controller_1_su), .A(reg_final_1_output), .B(xor_1_out), .OUTPUT(adder_1_output));
  REG_FINAL reg_final_2 (
    .INPUT({High, LOW}), .ENABLE(not_6_out), .CLK(controlled_buffer_4_out), .CLR(CLR),
    .OUTPUT(reg_final_2_output));
  REG_FINAL reg_final_3 (
    .INPUT({High, LOW}), .ENABLE(not_7_out), .CLK(controlled_buffer_4_out), .CLR(CLR),
    .OUTPUT(reg_final_3_output));
  not not_8 (not_8_out, controller_1_hlt);
  Clock Clk (.out(Clk_out));
  assign controlled_buffer_4_out = not_8_out ? Clk_out : 1'bz;  // Controlled_Buffer controlled_buffer_4
  assign xor_1_out = reg_final_2_output ^ bit_extender_1_out;  // XOR_Gate xor_1, 8 bits wide
  Hex_Digit_Display hex_digit_display_1 (.value(reg_final_3_output[7:4]));  // open: dp
  assign bit_extender_1_out = {{7{controller_1_su}}, controller_1_su};  // Bit_Extender bit_extender_1
  Hex_Digit_Display hex_digit_display_2 (.value(reg_final_3_output[3:0]));  // open: dp

  // Notes on the sheet:
  //   PC
  //   1607110
  //   MAR
  //   CONTROLLER
  //   RAM
  //   ACCUMULATOR
  //   ALU
  //   B REGISTER
  //   1607106
  //   OUTPUT REGISTER
endmodule

module decoder (
  input  I7,
  input  I6,
  input  I5,
  input  I4,
  output LDA,
  output ADD,
  output SUB,
  output OUT,
  output HLT
);

  wire and_1_out, and_2_out, and_3_out, and_4_out, and_5_out, not_1_out, not_2_out, not_3_out, not_4_out;

  not not_1 (not_1_out, I7);
  not not_2 (not_2_out, I6);
  not not_3 (not_3_out, I5);
  not not_4 (not_4_out, I4);
  and and_1 (and_1_out, not_1_out, not_2_out, not_3_out, not_4_out);
  and and_2 (and_2_out, not_1_out, not_2_out, not_3_out, I4);
  and and_3 (and_3_out, not_1_out, not_2_out, I5, not_4_out);
  and and_4 (and_4_out, I7, I6, I5, not_4_out);
  and and_5 (and_5_out, I7, I6, I5, I4);
  buf buffer_1 (LDA, and_1_out);
  buf buffer_2 (ADD, and_2_out);
  buf buffer_3 (SUB, and_3_out);
  buf buffer_4 (OUT, and_4_out);
  buf buffer_5 (HLT, and_5_out);

  // Notes on the sheet:
  //   1607110
endmodule

module CONTROLLER (
  input  CLK,
  input  CLR,
  input  I7,
  input  I6,
  input  I5,
  input  I4,
  output CP,
  output EP,
  output nLM,
  output nCE,
  output nL1,
  output nE1,
  output HLT,
  output nLA,
  output EA,
  output SU,
  output EU,
  output nLB,
  output nLO
);

  wire and_1_out, and_2_out, and_3_out, and_4_out, and_5_out, and_6_out, and_7_out, and_8_out, and_9_out,
       and_10_out, and_11_out, and_12_out, and_13_out, and_14_out, and_15_out, and_16_out, decoder_1_add,
       decoder_1_lda, decoder_1_out, decoder_1_sub, nand_1_out, nand_2_out, or_1_out, or_2_out, or_3_out,
       or_4_out, or_6_out, ringcounter_1_t3, ringcounter_1_t4, ringcounter_1_t5, ringcounter_1_t6;

  decoder decoder_1 (
    .I7(I7), .I6(I6), .I5(I5), .I4(I4), .LDA(decoder_1_lda), .ADD(decoder_1_add), .SUB(decoder_1_sub),
    .OUT(decoder_1_out), .HLT(HLT));
  and and_1 (and_1_out, decoder_1_lda, ringcounter_1_t4);
  and and_2 (and_2_out, decoder_1_add, ringcounter_1_t4);
  or or_1 (or_1_out, EP, and_1_out, and_2_out, and_3_out);
  not not_1 (nLM, or_1_out);
  and and_3 (and_3_out, decoder_1_sub, ringcounter_1_t4);
  and and_4 (and_4_out, decoder_1_lda, ringcounter_1_t5);
  and and_5 (and_5_out, decoder_1_add, ringcounter_1_t5);
  or or_2 (or_2_out, ringcounter_1_t3, and_4_out, and_5_out, and_6_out);
  not not_2 (nCE, or_2_out);
  and and_6 (and_6_out, decoder_1_sub, ringcounter_1_t5);
  not not_3 (nL1, ringcounter_1_t3);
  and and_7 (and_7_out, decoder_1_lda, ringcounter_1_t4);
  and and_8 (and_8_out, decoder_1_add, ringcounter_1_t4);
  or or_3 (or_3_out, and_7_out, and_8_out, and_9_out);
  not not_4 (nE1, or_3_out);
  and and_9 (and_9_out, decoder_1_sub, ringcounter_1_t4);
  and and_10 (and_10_out, decoder_1_lda, ringcounter_1_t5);
  RingCounter ringcounter_1 (
    .clk(CLK), .T6(ringcounter_1_t6), .T5(ringcounter_1_t5), .T4(ringcounter_1_t4), .T3(ringcounter_1_t3),
    .T2(CP), .T1(EP), .CLR(CLR));
  and and_11 (and_11_out, decoder_1_sub, ringcounter_1_t6);
  and and_12 (and_12_out, decoder_1_add, ringcounter_1_t6);
  or or_4 (or_4_out, and_10_out, and_12_out, and_11_out);
  not not_5 (nLA, or_4_out);
  nand nand_1 (nand_1_out, decoder_1_out, ringcounter_1_t4);
  not not_6 (EA, nand_1_out);
  nand nand_2 (nand_2_out, decoder_1_sub, ringcounter_1_t6);
  not not_7 (SU, nand_2_out);
  and and_13 (and_13_out, decoder_1_add, ringcounter_1_t6);
  and and_14 (and_14_out, decoder_1_sub, ringcounter_1_t6);
  or or_5 (EU, and_13_out, and_14_out);
  and and_15 (and_15_out, decoder_1_add, ringcounter_1_t5);
  and and_16 (and_16_out, decoder_1_sub, ringcounter_1_t5);
  or or_6 (or_6_out, and_15_out, and_16_out);
  not not_8 (nLB, or_6_out);
  nand nand_3 (nLO, ringcounter_1_t4, decoder_1_out);

  // Notes on the sheet:
  //   1607110
  //   1607106
endmodule

module memory_address_reg (
  input  x3,
  input  x2,
  input  x1,
  input  x0,
  input  LOAD,
  input  clr,
  input  clk,
  output y3,
  output y1,
  output y2,
  output y0
);

  wire and_1_out, and_2_out, and_3_out, and_4_out, and_5_out, and_6_out, and_7_out, and_8_out, d_ff_1_q,
       d_ff_2_q, d_ff_3_q, d_ff_4_q, not_1_out, or_1_out, or_2_out, or_3_out, or_4_out;

  assign y3 = 1'b1 ? d_ff_1_q : 1'bz;  // Controlled_Buffer controlled_buffer_1
  and and_1 (and_1_out, d_ff_1_q, not_1_out);
  or or_1 (or_1_out, and_1_out, and_2_out);
  D_Flip_Flop d_ff_1 (.clk(clk), .D(or_1_out), .Q(d_ff_1_q), .reset(clr));  // open: Qn, preset, en
  and and_2 (and_2_out, x3, LOAD);
  assign y2 = 1'b1 ? d_ff_2_q : 1'bz;  // Controlled_Buffer controlled_buffer_2
  and and_3 (and_3_out, d_ff_2_q, not_1_out);
  D_Flip_Flop d_ff_2 (.clk(clk), .D(or_2_out), .Q(d_ff_2_q), .reset(clr));  // open: Qn, preset, en
  and and_4 (and_4_out, x2, LOAD);
  or or_2 (or_2_out, and_3_out, and_4_out);
  assign y1 = 1'b1 ? d_ff_3_q : 1'bz;  // Controlled_Buffer controlled_buffer_3
  and and_5 (and_5_out, d_ff_3_q, not_1_out);
  D_Flip_Flop d_ff_3 (.clk(clk), .D(or_3_out), .Q(d_ff_3_q), .reset(clr));  // open: Qn, preset, en
  and and_6 (and_6_out, x1, LOAD);
  or or_3 (or_3_out, and_5_out, and_6_out);
  assign y0 = 1'b1 ? d_ff_4_q : 1'bz;  // Controlled_Buffer controlled_buffer_4
  not not_1 (not_1_out, LOAD);
  and and_7 (and_7_out, d_ff_4_q, not_1_out);
  or or_4 (or_4_out, and_7_out, and_8_out);
  D_Flip_Flop d_ff_4 (.clk(clk), .D(or_4_out), .Q(d_ff_4_q), .reset(clr));  // open: Qn, preset, en
  and and_8 (and_8_out, x0, LOAD);

  // Notes on the sheet:
  //   1607110
  //   ENABLE
endmodule

module RingCounter (
  input  clk,
  input  CLR,
  output T6,
  output T5,
  output T4,
  output T3,
  output T2,
  output T1
);

  wire j_k_ff_1_qn, j_k_ff_2_qn, j_k_ff_3_qn, j_k_ff_4_qn, j_k_ff_5_qn, j_k_ff_6_q, not_1_out;

  J_K_Flip_Flop j_k_ff_1 (
    .J(T5), .clk(not_1_out), .K(j_k_ff_2_qn), .Q(T6), .Qn(j_k_ff_1_qn), .reset(CLR));  // open: preset, en
  J_K_Flip_Flop j_k_ff_2 (
    .J(T4), .clk(not_1_out), .K(j_k_ff_3_qn), .Q(T5), .Qn(j_k_ff_2_qn), .reset(CLR));  // open: preset, en
  J_K_Flip_Flop j_k_ff_3 (
    .J(T3), .clk(not_1_out), .K(j_k_ff_4_qn), .Q(T4), .Qn(j_k_ff_3_qn), .reset(CLR));  // open: preset, en
  J_K_Flip_Flop j_k_ff_4 (
    .J(T2), .clk(not_1_out), .K(j_k_ff_5_qn), .Q(T3), .Qn(j_k_ff_4_qn), .reset(CLR));  // open: preset, en
  J_K_Flip_Flop j_k_ff_5 (
    .J(T1), .clk(not_1_out), .K(j_k_ff_6_q), .Q(T2), .Qn(j_k_ff_5_qn), .reset(CLR));  // open: preset, en
  not not_1 (not_1_out, clk);
  J_K_Flip_Flop j_k_ff_6 (
    .J(j_k_ff_1_qn), .clk(not_1_out), .K(T6), .Q(j_k_ff_6_q), .Qn(T1), .reset(CLR));  // open: preset, en

  // Notes on the sheet:
  //   1607106
endmodule

module TrueComplement (
  input  S0,
  input  B,
  input  S1,
  output Y
);

  wire and_1_out, and_2_out, not_1_out;

  not not_1 (not_1_out, B);
  and and_1 (and_1_out, S0, B);
  and and_2 (and_2_out, not_1_out, S1);
  or or_1 (Y, and_1_out, and_2_out);

  // Notes on the sheet:
  //   1607106
endmodule

module FA (
  input  digit1,
  input  digit2,
  input  carry_in,
  output S,
  output C
);

  wire and_1_out, and_2_out, xor_1_out;

  xor xor_1 (xor_1_out, digit1, digit2);
  and and_1 (and_1_out, digit1, digit2);
  xor xor_2 (S, xor_1_out, carry_in);
  and and_2 (and_2_out, xor_1_out, carry_in);
  or or_1 (C, and_2_out, and_1_out);

  // Notes on the sheet:
  //   1607106
endmodule

module ALU (
  input  Cin,
  input  A0,
  input  B0,
  input  A1,
  input  B1,
  input  A2,
  input  B2,
  input  A3,
  input  B3,
  input  A4,
  input  B4,
  input  A5,
  input  B5,
  input  A6,
  input  B6,
  input  A7,
  input  B7,
  output F0,
  output F1,
  output F2,
  output F3,
  output F4,
  output F5,
  output F6,
  output F7,
  output C_out
);

  wire fa_1_c, fa_2_c, fa_3_c, fa_4_c, fa_5_c, fa_6_c, fa_7_c, truecomplement_1_y, truecomplement_2_y,
       truecomplement_3_y, truecomplement_4_y, truecomplement_5_y, truecomplement_6_y, truecomplement_7_y,
       truecomplement_8_y;

  TrueComplement truecomplement_1 (.S0(1'b1), .B(B0), .S1(1'b0), .Y(truecomplement_1_y));
  TrueComplement truecomplement_2 (.S0(1'b1), .B(B1), .S1(1'b0), .Y(truecomplement_2_y));
  TrueComplement truecomplement_3 (.S0(1'b1), .B(B2), .S1(1'b0), .Y(truecomplement_3_y));
  TrueComplement truecomplement_4 (.S0(1'b1), .B(B3), .S1(1'b0), .Y(truecomplement_4_y));
  TrueComplement truecomplement_5 (.S0(1'b1), .B(B4), .S1(1'b0), .Y(truecomplement_5_y));
  TrueComplement truecomplement_6 (.S0(1'b1), .B(B5), .S1(1'b0), .Y(truecomplement_6_y));
  TrueComplement truecomplement_7 (.S0(1'b1), .B(B6), .S1(1'b0), .Y(truecomplement_7_y));
  TrueComplement truecomplement_8 (.S0(1'b1), .B(B7), .S1(1'b0), .Y(truecomplement_8_y));
  FA fa_1 (.digit1(A0), .digit2(truecomplement_1_y), .carry_in(Cin), .S(F0), .C(fa_1_c));
  FA fa_2 (.digit1(A1), .digit2(truecomplement_2_y), .carry_in(fa_1_c), .S(F1), .C(fa_2_c));
  FA fa_3 (.digit1(A2), .digit2(truecomplement_3_y), .carry_in(fa_2_c), .S(F2), .C(fa_3_c));
  FA fa_4 (.digit1(A3), .digit2(truecomplement_4_y), .carry_in(fa_3_c), .S(F3), .C(fa_4_c));
  FA fa_5 (.digit1(A4), .digit2(truecomplement_5_y), .carry_in(fa_4_c), .S(F4), .C(fa_5_c));
  FA fa_6 (.digit1(A5), .digit2(truecomplement_6_y), .carry_in(fa_5_c), .S(F5), .C(fa_6_c));
  FA fa_7 (.digit1(A6), .digit2(truecomplement_7_y), .carry_in(fa_6_c), .S(F6), .C(fa_7_c));
  FA fa_8 (.digit1(A7), .digit2(truecomplement_8_y), .carry_in(fa_7_c), .S(F7), .C(C_out));

  // Notes on the sheet:
  //   1607110
  //   LSB
  //   MSB
  //   S0
  //   S1
  //   LSB
  //   MSB
endmodule

module adder (
  input  cin,
  input  [7:0] A,
  input  [7:0] B,
  output [7:0] OUTPUT
);

  ALU alu_1 (
    .Cin(cin), .A0(A[0]), .B0(B[0]), .A1(A[1]), .B1(B[1]), .A2(A[2]), .B2(B[2]), .A3(A[3]), .B3(B[3]),
    .A4(A[4]), .B4(B[4]), .A5(A[5]), .B5(B[5]), .A6(A[6]), .B6(B[6]), .A7(A[7]), .B7(B[7]), .F0(OUTPUT[0]),
    .F1(OUTPUT[1]), .F2(OUTPUT[2]), .F3(OUTPUT[3]), .F4(OUTPUT[4]), .F5(OUTPUT[5]), .F6(OUTPUT[6]),
    .F7(OUTPUT[7]));  // open: C_out
endmodule

// 4_BIT
module MAR_FINAL (
  input  [3:0] IN,
  input  ENABLE,
  input  CLK,
  input  CLR,
  output [3:0] OUT
);

  memory_address_reg memory_address_reg_1 (
    .x3(IN[3]), .x2(IN[2]), .x1(IN[1]), .x0(IN[0]), .LOAD(ENABLE), .clr(CLR), .clk(CLK), .y3(OUT[3]),
    .y1(OUT[1]), .y2(OUT[2]), .y0(OUT[0]));
endmodule

module REG_FINAL (
  input  [7:0] INPUT,
  input  ENABLE,
  input  CLK,
  input  CLR,
  output [7:0] OUTPUT
);

  MAR_FINAL mar_final_1 (.IN(INPUT[3:0]), .ENABLE(ENABLE), .CLK(CLK), .CLR(CLR), .OUT(OUTPUT[3:0]));
  MAR_FINAL mar_final_2 (.IN(INPUT[7:4]), .ENABLE(ENABLE), .CLK(CLK), .CLR(CLR), .OUT(OUTPUT[7:4]));
endmodule

// PC
module pc (
  input  CP,
  input  EP,
  input  CLR,
  input  CLK,
  output [3:0] \output 
);

  wire j_k_ff_1_q, j_k_ff_2_q, j_k_ff_3_q, j_k_ff_4_q, not_1_out, not_2_out, not_3_out;

  not not_1 (not_1_out, j_k_ff_2_q);
  J_K_Flip_Flop j_k_ff_1 (.J(CP), .clk(not_1_out), .K(CP), .Q(j_k_ff_1_q), .preset(CLR));  // open: Qn, en, reset
  assign \output [3] = EP ? j_k_ff_1_q : 1'bz;  // Controlled_Buffer controlled_buffer_1
  not not_2 (not_2_out, j_k_ff_3_q);
  J_K_Flip_Flop j_k_ff_2 (.J(CP), .clk(not_2_out), .K(CP), .Q(j_k_ff_2_q), .preset(CLR));  // open: Qn, en, reset
  assign \output [2] = EP ? j_k_ff_2_q : 1'bz;  // Controlled_Buffer controlled_buffer_2
  not not_3 (not_3_out, j_k_ff_4_q);
  J_K_Flip_Flop j_k_ff_3 (.J(CP), .clk(not_3_out), .K(CP), .Q(j_k_ff_3_q), .preset(CLR));  // open: Qn, en, reset
  assign \output [1] = EP ? j_k_ff_3_q : 1'bz;  // Controlled_Buffer controlled_buffer_3
  J_K_Flip_Flop j_k_ff_4 (.J(CP), .clk(CLK), .K(CP), .Q(j_k_ff_4_q), .preset(CLR));  // open: Qn, en, reset
  assign \output [0] = EP ? j_k_ff_4_q : 1'bz;  // Controlled_Buffer controlled_buffer_4
endmodule
